// Logisim project ALU 1 bit.circ as structural Verilog: 1 circuit, main circuit ALU 1 bit
module ALU_1_bit (
  input  A,
  input  B,
  input  F1,
  input  F2,
  output Result,
  output Carry_PSW_Overflow
);

  wire A___B_out, A_AND_B_out, A_OR_B_out, and_1_out, and_2_out, and_3_out, and_4_out, and_5_out, and_6_out,
       and_7_out, not_1_out, not_2_out, NOT_A_out, xor_1_out;

  not not_1 (not_1_out, F2);
  not not_2 (not_2_out, F1);
  and A_AND_B (A_AND_B_out, A, B);
  or A_OR_B (A_OR_B_out, A, B);
  not NOT_A (NOT_A_out, A);
  and and_1 (and_1_out, F1, F2);
  and and_2 (and_2_out, F1, not_1_out);
  and and_3 (and_3_out, not_2_out, F2);
  and and_4 (and_4_out, not_2_out, not_1_out);
  and and_5 (and_5_out, A_AND_B_out, and_1_out);
  and and_6 (and_6_out, A_OR_B_out, and_2_out);
  and and_7 (and_7_out, NOT_A_out, and_3_out);
  and and_8 (Carry_PSW_Overflow, A, B);
  xor xor_1 (xor_1_out, A, B);
  and A___B (A___B_out, xor_1_out, and_4_out);
  or or_1 (Result, and_5_out, and_6_out, and_7_out, A___B_out);

  // Notes on the sheet:
  //   ALU 1 bit
endmodule
