// Logisim project Adder 4 bits.circ as structural Verilog: 1 circuit, main circuit Adder 4 bits
module Adder_4_bits (
  input  A1,
  input  B1,
  input  A2,
  input  B2,
  input  A3,
  input  B3,
  input  A4,
  input  B4,
  output _4__bit,
  output _3__bit,
  output _2__bit,
  output _1__bit,
  output Overflow_Flag_PSW
);

  wire and_1_out, and_2_out, and_3_out, and_4_out, and_5_out, and_6_out, and_7_out, or_1_out, or_2_out,
       xor_1_out, xor_2_out, xor_3_out;

  and and_1 (and_1_out, A1, B1);
  and and_2 (and_2_out, A2, B2);
  and and_3 (and_3_out, A3, B3);
  and and_4 (and_4_out, A4, B4);
  or or_1 (or_1_out, and_2_out, and_5_out);
  xor xor_1 (xor_1_out, A3, B3);
  or or_2 (or_2_out, and_3_out, and_6_out);
  xor xor_2 (xor_2_out, A4, B4);
  or or_3 (Overflow_Flag_PSW, and_4_out, and_7_out);
  xor xor_3 (xor_3_out, A2, B2);
  and and_5 (and_5_out, and_1_out, xor_3_out);
  and and_6 (and_6_out, or_1_out, xor_1_out);
  and and_7 (and_7_out, or_2_out, xor_2_out);
  xor xor_4 (_4__bit, A1, B1);
  xor xor_5 (_3__bit, and_1_out, xor_3_out);
  xor xor_6 (_2__bit, or_1_out, xor_1_out);
  xor xor_7 (_1__bit, or_2_out, xor_2_out);

  // Notes on the sheet:
  //   Adder 4 bits
endmodule
