// Logisim project Comparator 2 Strings of 4 bits.circ as structural Verilog: 1 circuit, main circuit Comparator 2 Strings of 4 bits
module Comparator_2_Strings_of_4_bits (
  input  A1,
  input  B1,
  input  A2,
  input  B2,
  input  A3,
  input  B3,
  input  A4,
  input  B4,
  output Output
);

  wire xor_1_out, xor_2_out, xor_3_out, xor_4_out;

  xor xor_1 (xor_1_out, A1, B1);
  xor xor_2 (xor_2_out, A2, B2);
  xor xor_3 (xor_3_out, A3, B3);
  xor xor_4 (xor_4_out, A4, B4);
  nor nor_1 (Output, xor_1_out, xor_2_out, xor_3_out, xor_4_out);

  // Notes on the sheet:
  //   Comparator 2 Strings of 4 bits
endmodule
