// Logisim project Comparator 3 Strings of 4 bits.circ as structural Verilog: 1 circuit, main circuit Comparator 3 Strings of 4 bits
module Comparator_3_Strings_of_4_bits (
  input  A1,
  input  B1,
  input  C1,
  input  A2,
  input  B2,
  input  C2,
  input  A3,
  input  B3,
  input  C3,
  input  A4,
  input  B4,
  input  C4,
  output Output
);

  wire xor_1_out, xor_2_out, xor_3_out, xor_4_out, xor_5_out, xor_6_out, xor_7_out, xor_8_out;

  xor xor_1 (xor_1_out, A1, B1);
  xor xor_2 (xor_2_out, B1, C1);
  xor xor_3 (xor_3_out, A2, B2);
  xor xor_4 (xor_4_out, B2, C2);
  xor xor_5 (xor_5_out, A3, B3);
  xor xor_6 (xor_6_out, B3, C3);
  xor xor_7 (xor_7_out, A4, B4);
  xor xor_8 (xor_8_out, B4, C4);
  nor nor_1 (Output, xor_1_out, xor_2_out, xor_3_out, xor_4_out, xor_5_out, xor_6_out, xor_7_out, xor_8_out);

  // Notes on the sheet:
  //   Comparator 3 Strings of 4 bits
endmodule
