// Logisim project Decoder 3 To 8.circ as structural Verilog: 1 circuit, main circuit Decoder 3
module Decoder_3 (
  input  A,
  input  B,
  input  C,
  output out_4,
  output out_5,
  output out_6,
  output out_7,
  output out_8,
  output out_9,
  output out_10,
  output out_11
);

  wire NOT_A_out, NOT_B_out, NOT_C_out;

  not NOT_A (NOT_A_out, A);
  not NOT_C (NOT_C_out, C);
  not NOT_B (NOT_B_out, B);
  and and_1 (out_4, A, B, C);
  and and_2 (out_5, A, B, NOT_C_out);
  and and_3 (out_6, A, NOT_B_out, C);
  and and_4 (out_7, A, NOT_B_out, NOT_C_out);
  and and_5 (out_8, NOT_A_out, B, C);
  and and_6 (out_9, NOT_A_out, B, NOT_C_out);
  and and_7 (out_10, NOT_A_out, NOT_B_out, C);
  and and_8 (out_11, NOT_A_out, NOT_B_out, NOT_C_out);

  // Notes on the sheet:
  //   Decoder 3 To 8
endmodule
