// Logisim project Demultiplexer1To8.circ as structural Verilog: 1 circuit, main circuit Demultiplexer 3 Ways
module Demultiplexer_3_Ways (
  input  D,
  input  A,
  input  B,
  input  C,
  output F0,
  output F1,
  output F2,
  output F3,
  output F4,
  output F5,
  output F6,
  output F7
);

  wire not_1_out, not_2_out, not_3_out;

  not not_1 (not_1_out, A);
  not not_2 (not_2_out, B);
  not not_3 (not_3_out, C);
  and and_1 (F0, D, A, B, C);
  and and_2 (F1, D, A, B, not_3_out);
  and and_3 (F2, D, A, not_2_out, C);
  and and_4 (F3, D, A, not_2_out, not_3_out);
  and and_5 (F4, D, not_1_out, B, C);
  and and_6 (F5, D, not_1_out, B, not_3_out);
  and and_7 (F6, D, not_1_out, not_2_out, C);
  and and_8 (F7, D, not_1_out, not_2_out, not_3_out);

  // Notes on the sheet:
  //   Demultiplexer 1 To 8
endmodule
