// Logisim project Enabled D Latch.circ as structural Verilog: 1 circuit, main circuit Enabled D Latch
module Enabled_D_Latch (
  input  D,
  output NOT_Q,
  output Q
);

  wire and_1_out, and_2_out, clock_1_out, not_1_out;

  Clock clock_1 (.out(clock_1_out));
  not not_1 (not_1_out, D);
  and and_1 (and_1_out, D, clock_1_out);
  and and_2 (and_2_out, clock_1_out, not_1_out);
  nor nor_1 (NOT_Q, and_1_out, Q);
  nor nor_2 (Q, NOT_Q, and_2_out);

  // Notes on the sheet:
  //   Enabled D Latch
endmodule
