// Logisim project Enabled SR Latch.circ as structural Verilog: 1 circuit, main circuit Enabled SR Latch
module Enabled_SR_Latch (
  input  S,
  input  S_2,
  input  R,
  input  R_2,
  output NOT_Q,
  output NOT_Q_2,
  output Q,
  output Q_2
);

  wire and_1_out, and_2_out, and_3_out, and_4_out, clock_1_out, clock_2_out;

  Clock clock_1 (.out(clock_1_out));
  and and_1 (and_1_out, S, clock_1_out);
  and and_2 (and_2_out, clock_1_out, R);
  nor nor_1 (NOT_Q, and_1_out, Q);
  nor nor_2 (Q, NOT_Q, and_2_out);
  Clock clock_2 (.out(clock_2_out));
  and and_3 (and_3_out, S_2, clock_2_out);
  and and_4 (and_4_out, clock_2_out, R_2);
  nand nand_1 (NOT_Q_2, and_3_out, Q_2);
  nand nand_2 (Q_2, NOT_Q_2, and_4_out);

  // Notes on the sheet:
  //   Enabled SR Latch LOW
  //   Enabled SR Latch HIGH
endmodule
