// Logisim project Flip-Flop D.circ as structural Verilog: 1 circuit, main circuit Flip-Flop D
module Flip_Flop_D (
  input  D,
  output NOT_Q,
  output Q
);

  wire and_1_out, and_2_out, and_3_out, Clock_out, not_1_out, not_2_out;

  Clock Clock (.out(Clock_out));
  not not_1 (not_1_out, Clock_out);
  and and_1 (and_1_out, not_1_out, Clock_out);
  not not_2 (not_2_out, D);
  and and_2 (and_2_out, D, and_1_out);
  and and_3 (and_3_out, and_1_out, not_2_out);
  nor nor_1 (NOT_Q, and_2_out, Q);
  nor nor_2 (Q, NOT_Q, and_3_out);

  // Notes on the sheet:
  //   Flip-Flop D
endmodule
