// Logisim project Full-Adder.circ as structural Verilog: 1 circuit, main circuit Full-Adder
module Full_Adder (
  input  Carry_Input,
  input  A,
  input  B,
  output Result,
  output Carry_Output
);

  wire and_1_out, and_2_out, xor_1_out;

  and and_1 (and_1_out, A, B);
  or or_1 (Carry_Output, and_1_out, and_2_out);
  xor xor_1 (xor_1_out, A, B);
  and and_2 (and_2_out, xor_1_out, Carry_Input);
  xor xor_2 (Result, Carry_Input, xor_1_out);

  // Notes on the sheet:
  //   Full-Adder
endmodule
