// Logisim project Half-Adder.circ as structural Verilog: 1 circuit, main circuit Half-Adder
module Half_Adder (
  input  A,
  input  B,
  output Result,
  output Carry
);

  and and_1 (Carry, A, B);
  xor xor_1 (Result, A, B);

  // Notes on the sheet:
  //   Half-Adder
endmodule
