// Logisim project Latch SR.circ as structural Verilog: 1 circuit, main circuit Latch SR
module Latch_SR (
  input  S,
  input  S_2,
  input  R,
  input  R_2,
  output NOT_Q,
  output NOT_Q_2,
  output Q,
  output Q_2
);

  nor nor_1 (NOT_Q, S, Q);
  nor nor_2 (Q, NOT_Q, R);
  nand nand_1 (NOT_Q_2, S_2, Q_2);
  nand nand_2 (Q_2, NOT_Q_2, R_2);

  // Notes on the sheet:
  //   Latch SR LOW
  //   Latch SR High
endmodule
