// Logisim project Memory 4x4 bit.circ as structural Verilog: 1 circuit, main circuit Memory 4x4 bit
module Memory_4x4_bit (
  input  I_3,
  input  I_2,
  input  I_1,
  input  I_0,
  input  A_0,
  input  A_1,
  input  CS,
  input  RD,
  input  OE,
  output O_3,
  output O_2,
  output O_1,
  output O_0
);

  wire and_1_out, and_2_out, and_3_out, and_4_out, and_5_out, and_6_out, and_7_out, and_8_out, and_9_out,
       and_10_out, and_11_out, and_12_out, and_13_out, and_14_out, and_15_out, and_16_out, and_17_out,
       and_18_out, and_19_out, and_20_out, and_21_out, and_22_out, and_23_out, and_24_out, and_25_out,
       and_26_out, d_ff_1_q, d_ff_2_q, d_ff_3_q, d_ff_4_q, d_ff_5_q, d_ff_6_q, d_ff_7_q, d_ff_8_q, d_ff_9_q,
       d_ff_10_q, d_ff_11_q, d_ff_12_q, d_ff_13_q, d_ff_14_q, d_ff_15_q, d_ff_16_q, not_1_out, not_2_out,
       not_3_out, or_1_out, or_2_out, or_3_out, or_4_out;

  not not_1 (not_1_out, A_0);
  not not_2 (not_2_out, A_1);
  and and_1 (and_1_out, not_1_out, not_2_out);
  and and_2 (and_2_out, not_1_out, A_1);
  and and_3 (and_3_out, A_0, not_2_out);
  and and_4 (and_4_out, A_0, A_1);
  and and_5 (and_5_out, and_1_out, and_9_out);
  and and_6 (and_6_out, and_2_out, and_9_out);
  and and_7 (and_7_out, and_3_out, and_9_out);
  and and_8 (and_8_out, and_4_out, and_9_out);
  and and_9 (and_9_out, CS, not_3_out);
  not not_3 (not_3_out, RD);
  D_Flip_Flop d_ff_1 (.clk(and_5_out), .D(I_0), .Q(d_ff_1_q));  // open: Qn, preset, en, reset
  D_Flip_Flop d_ff_2 (.clk(and_6_out), .D(I_0), .Q(d_ff_2_q));  // open: Qn, preset, en, reset
  D_Flip_Flop d_ff_3 (.clk(and_7_out), .D(I_0), .Q(d_ff_3_q));  // open: Qn, preset, en, reset
  D_Flip_Flop d_ff_4 (.clk(and_8_out), .D(I_0), .Q(d_ff_4_q));  // open: Qn, preset, en, reset
  and and_10 (and_10_out, RD, CS, OE);
  and and_11 (and_11_out, d_ff_1_q, and_1_out);
  and and_12 (and_12_out, d_ff_2_q, and_2_out);
  and and_13 (and_13_out, d_ff_3_q, and_3_out);
  and and_14 (and_14_out, d_ff_4_q, and_4_out);
  or or_1 (or_1_out, and_14_out, and_13_out, and_12_out, and_11_out);
  D_Flip_Flop d_ff_5 (.clk(and_5_out), .D(I_1), .Q(d_ff_5_q));  // open: Qn, preset, en, reset
  D_Flip_Flop d_ff_6 (.clk(and_6_out), .D(I_1), .Q(d_ff_6_q));  // open: Qn, preset, en, reset
  D_Flip_Flop d_ff_7 (.clk(and_7_out), .D(I_1), .Q(d_ff_7_q));  // open: Qn, preset, en, reset
  and and_15 (and_15_out, d_ff_7_q, and_3_out);
  D_Flip_Flop d_ff_8 (.clk(and_8_out), .D(I_1), .Q(d_ff_8_q));  // open: Qn, preset, en, reset
  and and_16 (and_16_out, d_ff_8_q, and_4_out);
  and and_17 (and_17_out, d_ff_5_q, and_1_out);
  and and_18 (and_18_out, d_ff_6_q, and_2_out);
  or or_2 (or_2_out, and_16_out, and_15_out, and_18_out, and_17_out);
  D_Flip_Flop d_ff_9 (.clk(and_5_out), .D(I_2), .Q(d_ff_9_q));  // open: Qn, preset, en, reset
  D_Flip_Flop d_ff_10 (.clk(and_6_out), .D(I_2), .Q(d_ff_10_q));  // open: Qn, preset, en, reset
  D_Flip_Flop d_ff_11 (.clk(and_7_out), .D(I_2), .Q(d_ff_11_q));  // open: Qn, preset, en, reset
  D_Flip_Flop d_ff_12 (.clk(and_8_out), .D(I_2), .Q(d_ff_12_q));  // open: Qn, preset, en, reset
  and and_19 (and_19_out, d_ff_9_q, and_1_out);
  and and_20 (and_20_out, d_ff_10_q, and_2_out);
  and and_21 (and_21_out, d_ff_11_q, and_3_out);
  and and_22 (and_22_out, d_ff_12_q, and_4_out);
  or or_3 (or_3_out, and_22_out, and_21_out, and_20_out, and_19_out);
  assign O_0 = and_10_out ? or_1_out : 1'bz;  // Controlled_Buffer controlled_buffer_1
  D_Flip_Flop d_ff_13 (.clk(and_5_out), .D(I_3), .Q(d_ff_13_q));  // open: Qn, preset, en, reset
  D_Flip_Flop d_ff_14 (.clk(and_6_out), .D(I_3), .Q(d_ff_14_q));  // open: Qn, preset, en, reset
  D_Flip_Flop d_ff_15 (.clk(and_7_out), .D(I_3), .Q(d_ff_15_q));  // open: Qn, preset, en, reset
  and and_23 (and_23_out, d_ff_15_q, and_3_out);
  D_Flip_Flop d_ff_16 (.clk(and_8_out), .D(I_3), .Q(d_ff_16_q));  // open: Qn, preset, en, reset
  and and_24 (and_24_out, d_ff_16_q, and_4_out);
  assign O_2 = and_10_out ? or_3_out : 1'bz;  // Controlled_Buffer controlled_buffer_2
  assign O_1 = and_10_out ? or_2_out : 1'bz;  // Controlled_Buffer controlled_buffer_3
  and and_25 (and_25_out, d_ff_13_q, and_1_out);
  and and_26 (and_26_out, d_ff_14_q, and_2_out);
  or or_4 (or_4_out, and_24_out, and_23_out, and_26_out, and_25_out);
  assign O_3 = and_10_out ? or_4_out : 1'bz;  // Controlled_Buffer controlled_buffer_4

  // Notes on the sheet:
  //   Memory 4x4 bit
endmodule
