// Logisim project Multiplexer3Ways.circ as structural Verilog: 1 circuit, main circuit Multiplexer 3 ways
module Multiplexer_3_ways (
  input  D0,
  input  D1,
  input  D2,
  input  D3,
  input  D4,
  input  D5,
  input  D6,
  input  D7,
  input  A,
  input  B,
  input  C,
  output F
);

  wire and_1_out, and_2_out, and_3_out, and_4_out, and_5_out, and_6_out, and_7_out, and_8_out, NOT_A_out,
       NOT_B_out, NOT_C_out;

  not NOT_A (NOT_A_out, A);
  not NOT_B (NOT_B_out, B);
  not NOT_C (NOT_C_out, C);
  and and_1 (and_1_out, D0, A, B, C);
  and and_2 (and_2_out, D1, A, B, NOT_C_out);
  and and_3 (and_3_out, D2, A, NOT_B_out, C);
  and and_4 (and_4_out, D3, A, NOT_B_out, NOT_C_out);
  and and_5 (and_5_out, D4, NOT_A_out, B, C);
  and and_6 (and_6_out, D5, NOT_A_out, B, NOT_C_out);
  and and_7 (and_7_out, D6, NOT_A_out, NOT_B_out, C);
  and and_8 (and_8_out, D7, NOT_A_out, NOT_B_out, NOT_C_out);
  or or_1 (F, and_1_out, and_2_out, and_3_out, and_4_out, and_5_out, and_6_out, and_7_out, and_8_out);

  // Notes on the sheet:
  //   Multiplexer 3 Ways
endmodule
