// Logisim project Register 8 bit.circ as structural Verilog: 1 circuit, main circuit Register 8 bit
module Register_8_bit (
  input  I_0,
  input  I_1,
  input  I_2,
  input  I_3,
  input  Clear,
  input  I_4,
  input  I_5,
  input  I_6,
  input  I_7,
  input  I_0_2,
  input  I_1_2,
  input  I_2_2,
  input  I_3_2,
  input  I_4_2,
  input  I_5_2,
  input  I_6_2,
  input  I_7_2,
  output O_0,
  output O_1,
  output O_2,
  output O_3,
  output O_4,
  output O_5,
  output O_6,
  output O_7,
  output O_0_2,
  output O_1_2,
  output O_2_2,
  output O_3_2,
  output O_4_2,
  output O_5_2,
  output O_6_2,
  output O_7_2
);

  wire and_1_out, and_2_out, and_3_out, and_4_out, and_5_out, and_6_out, and_7_out, and_8_out, and_9_out,
       and_10_out, and_11_out, and_12_out, and_13_out, and_14_out, and_15_out, and_16_out, and_17_out,
       clock_1_out, clock_2_out, nor_1_out, nor_3_out, nor_5_out, nor_7_out, nor_9_out, nor_11_out,
       nor_13_out, nor_15_out, not_1_out, not_2_out, not_3_out, not_4_out, not_5_out, not_6_out, not_7_out,
       not_8_out, not_9_out;

  Clock clock_1 (.out(clock_1_out));
  not not_1 (not_1_out, clock_1_out);
  and and_1 (and_1_out, not_1_out, clock_1_out);
  Clock clock_2 (.out(clock_2_out));
  D_Flip_Flop d_ff_1 (.clk(clock_2_out), .D(I_0), .Q(O_0), .reset(Clear));  // open: Qn, preset, en
  D_Flip_Flop d_ff_2 (.clk(clock_2_out), .D(I_4), .Q(O_4), .reset(Clear));  // open: Qn, preset, en
  D_Flip_Flop d_ff_3 (.clk(clock_2_out), .D(I_1), .Q(O_1), .reset(Clear));  // open: Qn, preset, en
  and and_2 (and_2_out, I_0_2, and_1_out);
  and and_3 (and_3_out, and_1_out, not_2_out);
  not not_2 (not_2_out, I_0_2);
  and and_4 (and_4_out, I_1_2, and_1_out);
  and and_5 (and_5_out, and_1_out, not_3_out);
  not not_3 (not_3_out, I_1_2);
  and and_6 (and_6_out, I_2_2, and_1_out);
  and and_7 (and_7_out, and_1_out, not_4_out);
  not not_4 (not_4_out, I_2_2);
  and and_8 (and_8_out, I_3_2, and_1_out);
  and and_9 (and_9_out, and_1_out, not_5_out);
  not not_5 (not_5_out, I_3_2);
  and and_10 (and_10_out, I_4_2, and_1_out);
  and and_11 (and_11_out, and_1_out, not_6_out);
  not not_6 (not_6_out, I_4_2);
  and and_12 (and_12_out, I_5_2, and_1_out);
  and and_13 (and_13_out, and_1_out, not_7_out);
  not not_7 (not_7_out, I_5_2);
  and and_14 (and_14_out, I_6_2, and_1_out);
  and and_15 (and_15_out, and_1_out, not_8_out);
  not not_8 (not_8_out, I_6_2);
  and and_16 (and_16_out, I_7_2, and_1_out);
  and and_17 (and_17_out, and_1_out, not_9_out);
  not not_9 (not_9_out, I_7_2);
  D_Flip_Flop d_ff_4 (.clk(clock_2_out), .D(I_5), .Q(O_5), .reset(Clear));  // open: Qn, preset, en
  nor nor_1 (nor_1_out, and_2_out, O_0_2);
  nor nor_2 (O_0_2, nor_1_out, and_3_out);
  nor nor_3 (nor_3_out, and_4_out, O_1_2);
  nor nor_4 (O_1_2, nor_3_out, and_5_out);
  nor nor_5 (nor_5_out, and_6_out, O_2_2);
  nor nor_6 (O_2_2, nor_5_out, and_7_out);
  nor nor_7 (nor_7_out, and_8_out, O_3_2);
  nor nor_8 (O_3_2, nor_7_out, and_9_out);
  nor nor_9 (nor_9_out, and_10_out, O_4_2);
  nor nor_10 (O_4_2, nor_9_out, and_11_out);
  nor nor_11 (nor_11_out, and_12_out, O_5_2);
  nor nor_12 (O_5_2, nor_11_out, and_13_out);
  nor nor_13 (nor_13_out, and_14_out, O_6_2);
  nor nor_14 (O_6_2, nor_13_out, and_15_out);
  nor nor_15 (nor_15_out, and_16_out, O_7_2);
  nor nor_16 (O_7_2, nor_15_out, and_17_out);
  D_Flip_Flop d_ff_5 (.clk(clock_2_out), .D(I_2), .Q(O_2), .reset(Clear));  // open: Qn, preset, en
  D_Flip_Flop d_ff_6 (.clk(clock_2_out), .D(I_6), .Q(O_6), .reset(Clear));  // open: Qn, preset, en
  D_Flip_Flop d_ff_7 (.clk(clock_2_out), .D(I_3), .Q(O_3), .reset(Clear));  // open: Qn, preset, en
  D_Flip_Flop d_ff_8 (.clk(clock_2_out), .D(I_7), .Q(O_7), .reset(Clear));  // open: Qn, preset, en

  // Notes on the sheet:
  //   Register 8 bit
  //   Register 8 bit without Clear
endmodule
